// Logisim project DrawCPU-8.circ as structural Verilog
module HalfAdder (
  input  A,
  input  B,
  output S,
  output C
);

  Mera_XOR mera_xor_1 (.A(A), .B(B), .O(S));
  and and_1 (C, B, A);
endmodule

module FullAdder (
  input  A,
  input  B,
  input  Cin,
  output S,
  output Cout
);

  wire halfadder_1_c, halfadder_1_s, halfadder_2_c;

  HalfAdder halfadder_1 (.A(A), .B(B), .S(halfadder_1_s), .C(halfadder_1_c));
  or or_1 (Cout, halfadder_1_c, halfadder_2_c);
  HalfAdder halfadder_2 (.A(halfadder_1_s), .B(Cin), .S(S), .C(halfadder_2_c));
endmodule

module Mera_XOR (
  input  A,
  input  B,
  output O
);

  wire and_1_out, and_2_out, not_1_out, not_2_out;

  not not_1 (not_1_out, A);
  not not_2 (not_2_out, B);
  and and_1 (and_1_out, not_1_out, B);
  and and_2 (and_2_out, not_2_out, A);
  or or_1 (O, and_1_out, and_2_out);
endmodule

module FFA (
  input  [3:0] A,
  input  [3:0] B,
  input  Cin,
  output [3:0] S,
  output Cout
);

  wire fulladder_1_cout, fulladder_2_cout, fulladder_3_cout;

  FullAdder fulladder_1 (.A(A[0]), .B(B[0]), .Cin(Cin), .S(S[0]), .Cout(fulladder_1_cout));
  FullAdder fulladder_2 (.A(A[2]), .B(B[2]), .Cin(fulladder_3_cout), .S(S[2]), .Cout(fulladder_2_cout));
  FullAdder fulladder_3 (.A(A[1]), .B(B[1]), .Cin(fulladder_1_cout), .S(S[1]), .Cout(fulladder_3_cout));
  FullAdder fulladder_4 (.A(A[3]), .B(B[3]), .Cin(fulladder_2_cout), .S(S[3]), .Cout(Cout));
endmodule

module EFA (
  input  [7:0] A,
  input  [7:0] B,
  input  Cin,
  output [7:0] Sum,
  output Cout
);

  wire ffa_1_cout;

  FFA ffa_1 (.A(A[3:0]), .B(B[3:0]), .Cin(Cin), .S(Sum[3:0]), .Cout(ffa_1_cout));
  FFA ffa_2 (.A(A[7:4]), .B(B[7:4]), .Cin(ffa_1_cout), .S(Sum[7:4]), .Cout(Cout));
endmodule

module AU (
  input  [7:0] A,
  input  [7:0] B,
  input  SE,
  output [7:0] S_D
);

  wire efa_1_cout;
  wire [7:0] mera_xor_3_o;

  Mera_XOR mera_xor_1 (.A(SE), .B(B[4]), .O(mera_xor_3_o[4]));
  Mera_XOR mera_xor_2 (.A(SE), .B(B[5]), .O(mera_xor_3_o[5]));
  Mera_XOR mera_xor_3 (.A(SE), .B(B[0]), .O(mera_xor_3_o[0]));
  Mera_XOR mera_xor_4 (.A(SE), .B(B[1]), .O(mera_xor_3_o[1]));
  Mera_XOR mera_xor_5 (.A(SE), .B(B[2]), .O(mera_xor_3_o[2]));
  Mera_XOR mera_xor_6 (.A(SE), .B(B[3]), .O(mera_xor_3_o[3]));
  Mera_XOR mera_xor_7 (.A(SE), .B(B[6]), .O(mera_xor_3_o[6]));
  EFA efa_1 (.A(A), .B(mera_xor_3_o), .Cin(SE), .Sum(S_D), .Cout(efa_1_cout));
  Mera_XOR mera_xor_8 (.A(SE), .B(B[7]), .O(mera_xor_3_o[7]));
  // NoConnect on efa_1_cout
endmodule

module ALU (
  input  [7:0] A,
  input  [7:0] B,
  input  SE,
  input  [2:0] SEL,
  output [7:0] O
);

  wire [7:0] and_1_out, au_1_s_d, mera_xor_8_1_o, nand_1_out, nor_1_out, not_1_out, not_2_out, or_1_out;

  assign not_1_out = ~B;  // NOT_Gate not_1, 8 bits wide
  AU au_1 (.A(A), .B(B), .SE(SE), .S_D(au_1_s_d));
  Mera_XOR_8 mera_xor_8_1 (.A(A), .B(B), .O(mera_xor_8_1_o));
  Multiplexer #(.select(3), .width(8)) multiplexer_1 (
    .in0(au_1_s_d), .in1(not_2_out), .in2(and_1_out), .in3(mera_xor_8_1_o), .in4(or_1_out), .in5(nand_1_out),
    .in6(nor_1_out), .in7(not_1_out), .out(O), .sel(SEL));
  assign and_1_out = A & B;  // AND_Gate and_1, 8 bits wide
  assign not_2_out = ~A;  // NOT_Gate not_2, 8 bits wide
  assign or_1_out = A | B;  // OR_Gate or_1, 8 bits wide
  assign nand_1_out = ~(A & B);  // NAND_Gate nand_1, 8 bits wide
  assign nor_1_out = ~(A | B);  // NOR_Gate nor_1, 8 bits wide
endmodule

module Mera_XOR_8 (
  input  [7:0] A,
  input  [7:0] B,
  output [7:0] O
);

  wire [7:0] and_1_out, and_2_out, not_1_out, not_2_out;

  assign not_1_out = ~A;  // NOT_Gate not_1, 8 bits wide
  assign not_2_out = ~B;  // NOT_Gate not_2, 8 bits wide
  assign and_1_out = not_1_out & B;  // AND_Gate and_1, 8 bits wide
  assign and_2_out = not_2_out & A;  // AND_Gate and_2, 8 bits wide
  assign O = and_1_out | and_2_out;  // OR_Gate or_1, 8 bits wide
endmodule

module SR_Latch (
  input  R,
  input  S,
  output Q,
  output Q_NOT
);

  nor nor_1 (Q, Q_NOT, R);
  nor nor_2 (Q_NOT, Q, S);
endmodule

module D_Latch (
  input  D,
  input  EN,
  output Q,
  output Q_NOT
);

  wire and_1_out, and_2_out, not_1_out;

  not not_1 (not_1_out, D);
  and and_1 (and_1_out, not_1_out, EN);
  and and_2 (and_2_out, EN, D);
  SR_Latch sr_latch_1 (.R(and_1_out), .S(and_2_out), .Q(Q), .Q_NOT(Q_NOT));
endmodule

module D_FlipFlop (
  input  D,
  input  CLK,
  output Q,
  output Q_NOT
);

  D_Flip_Flop d_ff_1 (.D(D), .clk(CLK), .Q(Q), .Qn(Q_NOT));  // open: preset, reset
endmodule

module Mera_Register (
  input  LD,
  input  D,
  input  CLK,
  input  EN,
  output Q,
  output BS
);

  wire and_1_out, and_2_out, d_flipflop_1_q_not, not_1_out, or_1_out;

  not not_1 (not_1_out, LD);
  and and_1 (and_1_out, not_1_out, Q);
  and and_2 (and_2_out, LD, D);
  or or_1 (or_1_out, and_1_out, and_2_out);
  assign BS = EN ? Q : 1'bz;  // Controlled_Buffer controlled_buffer_1
  D_FlipFlop d_flipflop_1 (.D(or_1_out), .CLK(CLK), .Q(Q), .Q_NOT(d_flipflop_1_q_not));
  // NoConnect on d_flipflop_1_q_not
endmodule
